// Logisim project Final_Project.circ as structural Verilog: 15 circuits, main circuit main
module main (
  input  clk,
  input  reset,
  output [3:0] Y
);

  wire d_ff_1_qn, d_ff_2_qn, d_ff_3_qn, d_ff_4_qn;

  D_Flip_Flop d_ff_1 (.D(d_ff_1_qn), .clk(clk), .Q(Y[0]), .Qn(d_ff_1_qn), .reset(reset));  // open: preset
  D_Flip_Flop d_ff_2 (.D(d_ff_2_qn), .clk(d_ff_1_qn), .Q(Y[1]), .Qn(d_ff_2_qn), .reset(reset));  // open: preset
  D_Flip_Flop d_ff_3 (.D(d_ff_3_qn), .clk(d_ff_2_qn), .Q(Y[2]), .Qn(d_ff_3_qn), .reset(reset));  // open: preset
  D_Flip_Flop d_ff_4 (.D(d_ff_4_qn), .clk(d_ff_3_qn), .Q(Y[3]), .Qn(d_ff_4_qn));  // open: preset, reset
endmodule

module OneBitAdder (
  input  C_in,
  input  A,
  input  B,
  output S,
  output C_out
);

  wire and_1_out, and_2_out, and_3_out, or_1_out, xor_1_out;

  xor xor_1 (xor_1_out, A, B);
  and and_1 (and_1_out, A, B);
  and and_2 (and_2_out, A, C_in);
  and and_3 (and_3_out, B, C_in);
  xor xor_2 (S, C_in, xor_1_out);
  or or_1 (or_1_out, and_1_out, and_2_out);
  or or_2 (C_out, or_1_out, and_3_out);
endmodule

module FourBitAdder (
  input  C_in,
  input  [3:0] A,
  input  [3:0] B,
  output [3:0] Sum,
  output C_out
);

  wire onebitadder_1_c_out, onebitadder_2_c_out, onebitadder_3_c_out;

  OneBitAdder onebitadder_1 (.C_in(C_in), .A(A[0]), .B(B[0]), .S(Sum[0]), .C_out(onebitadder_1_c_out));
  OneBitAdder onebitadder_2 (.C_in(onebitadder_1_c_out), .A(A[1]), .B(B[1]), .S(Sum[1]), .C_out(onebitadder_2_c_out));
  OneBitAdder onebitadder_3 (.C_in(onebitadder_2_c_out), .A(A[2]), .B(B[2]), .S(Sum[2]), .C_out(onebitadder_3_c_out));
  OneBitAdder onebitadder_4 (.C_in(onebitadder_3_c_out), .A(A[3]), .B(B[3]), .S(Sum[3]), .C_out(C_out));
endmodule

module ALU (
  input  in_1,
  input  [3:0] A,
  input  [3:0] c_in_multiplyer,
  input  [3:0] B,
  input  [2:0] OP,
  input  in_6,
  output C_OUT_SUM,
  output [3:0] Result,
  output [3:0] c_out_multiply,
  output subtractor_bit
);

  wire [0:0] comparator_1_eq, comparator_1_gt, comparator_1_lt;
  wire [3:0] fourbitadder_1_sum, fourbitsubtractor_1_s, multiplier_1_out;

  FourBitAdder fourbitadder_1 (.C_in(in_1), .A(A), .B(B), .Sum(fourbitadder_1_sum), .C_out(C_OUT_SUM));
  FourBitSubtractor fourbitsubtractor_1 (.C_in(in_6), .A(A), .B(B), .S(fourbitsubtractor_1_s), .out_5(subtractor_bit));
  Multiplier #(.width(4)) multiplier_1 (
    .a(A), .b(B), .out(multiplier_1_out), .cin(c_in_multiplyer), .cout(c_out_multiply));
  Comparator #(.width(4)) comparator_1 (
    .a(A), .b(B), .gt(comparator_1_gt[0]), .eq(comparator_1_eq[0]), .lt(comparator_1_lt[0]));
  Multiplexer #(.select(3), .width(4)) multiplexer_1 (
    .in1(fourbitadder_1_sum), .in2(fourbitsubtractor_1_s), .in3({3'b000, comparator_1_gt[0]}),
    .in4({3'b000, comparator_1_eq[0]}), .in5({3'b000, comparator_1_lt[0]}), .in6(multiplier_1_out),
    .out(Result), .sel(OP));  // open: in0, in7
endmodule

module FourBitSubtractor (
  input  C_in,
  input  [3:0] A,
  input  [3:0] B,
  output [3:0] S,
  output out_5
);

  wire fourbitadder_1_c_out, undriven;
  wire [3:0] fourbitadder_1_sum, not_1_out;

  assign not_1_out = ~B;  // NOT_Gate not_1, 4 bits wide
  FourBitAdder fourbitadder_1 (
    .C_in(C_in), .A(A), .B(not_1_out), .Sum(fourbitadder_1_sum), .C_out(fourbitadder_1_c_out));
  FourBitAdder fourbitadder_2 (.C_in(undriven), .A(fourbitadder_1_sum), .B(4'b0001), .Sum(S), .C_out(out_5));
endmodule

module Splitters (
  input  [3:0] in_1,
  input  [3:0] in_2,
  output [7:0] out_3
);


  assign out_3 = {in_2, in_1};
endmodule

module FSM1 (
  input  Reset,
  input  cntrEnable,
  input  CLK,
  output s0,
  output s1,
  output s2
);

  wire counter_1_carry, not_1_out, not_2_out;

  not not_1 (not_1_out, Reset);
  Counter #(.max('h4), .width(3)) counter_1 (
    .clr(Reset), .load(Reset), .up(not_1_out), .count(cntrEnable), .clk(CLK), .carry(counter_1_carry));  // open: D, Q
  Counter #(.max('h4), .width(3)) counter_2 (
    .clr(Reset), .load(Reset), .up(not_2_out), .count(cntrEnable), .clk(counter_1_carry), .Q({s2, s1, s0}));  // open: D, carry
  not not_2 (not_2_out, Reset);
endmodule

module FSM2 (
  input  Reset,
  input  enabler,
  input  CLK,
  output readSelect,
  output writeSelect,
  output Reg1WE,
  output Reg2WE,
  output Reg3WE,
  output DMread,
  output DMwrite,
  output Resilt_1_2,
  output reset1,
  output ENabler_re
);

  wire fsm1_1_s0, fsm1_1_s1, fsm1_1_s2, not_1_out, not_2_out;

  not not_1 (not_1_out, fsm1_1_s2);
  not not_2 (not_2_out, fsm1_1_s0);
  not not_3 (DMread, fsm1_1_s1);
  and and_1 (writeSelect, not_1_out, fsm1_1_s1);
  and and_2 (DMwrite, not_1_out, fsm1_1_s1);
  and and_3 (readSelect, fsm1_1_s0, not_1_out, DMread);
  and and_4 (Reg1WE, DMread, not_1_out, not_2_out);
  and and_5 (Reg2WE, fsm1_1_s0, not_1_out, DMread);
  and and_6 (Reg3WE, not_2_out, not_1_out, fsm1_1_s1);
  and and_7 (Resilt_1_2, fsm1_1_s1, not_1_out, fsm1_1_s0);
  and and_8 (reset1, fsm1_1_s2, DMread, not_2_out);
  and and_9 (ENabler_re, ~fsm1_1_s2, fsm1_1_s1);  // AND_Gate
  FSM1 fsm1_1 (.Reset(Reset), .cntrEnable(enabler), .CLK(CLK), .s0(fsm1_1_s0), .s1(fsm1_1_s1), .s2(fsm1_1_s2));
endmodule

module four_bit_counter (
  input  CLK,
  input  reset,
  output [3:0] Y
);

  wire d_ff_1_qn, d_ff_2_qn, d_ff_3_qn, d_ff_4_qn;

  D_Flip_Flop d_ff_1 (.D(d_ff_1_qn), .clk(CLK), .Q(Y[0]), .Qn(d_ff_1_qn), .reset(reset));  // open: preset
  D_Flip_Flop d_ff_2 (.D(d_ff_2_qn), .clk(d_ff_1_qn), .Q(Y[1]), .Qn(d_ff_2_qn), .reset(reset));  // open: preset
  D_Flip_Flop d_ff_3 (.D(d_ff_3_qn), .clk(d_ff_2_qn), .Q(Y[2]), .Qn(d_ff_3_qn), .reset(reset));  // open: preset
  D_Flip_Flop d_ff_4 (.D(d_ff_4_qn), .clk(d_ff_3_qn), .Q(Y[3]), .Qn(d_ff_4_qn), .reset(reset));  // open: preset
endmodule

module three_bit_counter (
  input  CLK,
  input  reset,
  output [2:0] Y
);

  wire d_ff_1_qn, d_ff_2_qn, d_ff_3_qn;

  D_Flip_Flop d_ff_1 (.D(d_ff_1_qn), .clk(CLK), .Q(Y[0]), .Qn(d_ff_1_qn), .reset(reset));  // open: preset
  D_Flip_Flop d_ff_2 (.D(d_ff_2_qn), .clk(d_ff_1_qn), .Q(Y[1]), .Qn(d_ff_2_qn), .reset(reset));  // open: preset
  D_Flip_Flop d_ff_3 (.D(d_ff_3_qn), .clk(d_ff_2_qn), .Q(Y[2]), .Qn(d_ff_3_qn), .reset(reset));  // open: preset
endmodule

module forcounter (
  input  Reset,
  input  cntrEnable,
  input  CLK,
  output [2:0] Y
);

  wire counter_1_carry;

  Counter #(.max('h18), .width(5)) counter_1 (
    .clr(Reset), .load(Reset), .up(cntrEnable), .count(cntrEnable), .clk(CLK), .carry(counter_1_carry));  // open: D, Q
  three_bit_counter three_bit_counter_1 (.CLK(counter_1_carry), .reset(Reset), .Y(Y));
endmodule

module a_counter (
  input  Reset,
  input  Enabler,
  input  clk,
  output out_put
);

  wire not_1_out;
  wire [3:0] undriven;

  Counter #(.max('h4), .width(4)) counter_1 (
    .clr(Reset), .load(Reset), .up(not_1_out), .count(Enabler), .clk(clk), .D(undriven), .carry(out_put));  // open: Q
  not not_1 (not_1_out, Reset);
endmodule

module test_counter (
  input  Reset,
  input  clk,
  input  en,
  output [3:0] out_4
);

  wire not_1_out;
  wire [3:0] counter_1_q;

  Counter #(.max('hf), .width(4)) counter_1 (
    .clr(Reset), .load(Reset), .up(not_1_out), .count(en), .clk(clk), .Q(counter_1_q));  // open: D, carry
  not not_1 (not_1_out, Reset);
  FourBitAdder fourbitadder_1 (.A(4'b0010), .B(counter_1_q), .Sum(out_4));  // open: C_in, C_out
endmodule

module Register_File (
  input  WE,
  input  Reset,
  input  CLK,
  input  [3:0] Y,
  input  [2:0] OP_Code,
  output [3:0] Q
);

  wire [3:0] demultiplexer_1_out1, demultiplexer_1_out2, demultiplexer_1_out3, demultiplexer_1_out4,
       demultiplexer_1_out5, demultiplexer_1_out6, Equal_to_q, greater_than_q, Lesser_than_q, Subtract_q,
       Sum_q;

  Demultiplexer #(.select(3), .width(4)) demultiplexer_1 (
    .out1(demultiplexer_1_out1), .out2(demultiplexer_1_out2), .out3(demultiplexer_1_out3),
    .out4(demultiplexer_1_out4), .out5(demultiplexer_1_out5), .out6(demultiplexer_1_out6), .in(Y),
    .sel(OP_Code));  // open: out0, out7
  Register #(.width(4)) Sum (.D(demultiplexer_1_out1), .en(WE), .clk(CLK), .Q(Sum_q), .clr(Reset));
  Register #(.width(4)) Subtract (.D(demultiplexer_1_out2), .en(WE), .clk(CLK), .Q(Subtract_q), .clr(Reset));
  Register #(.width(4)) greater_than (.D(demultiplexer_1_out3), .en(WE), .clk(CLK), .Q(greater_than_q), .clr(Reset));
  Register #(.width(4)) Equal_to (.D(demultiplexer_1_out4), .en(WE), .clk(CLK), .Q(Equal_to_q), .clr(Reset));
  Register #(.width(4)) Lesser_than (.D(demultiplexer_1_out5), .en(WE), .clk(CLK), .Q(Lesser_than_q), .clr(Reset));
  Multiplexer #(.select(3), .width(4)) multiplexer_1 (
    .in1(Sum_q), .in2(Subtract_q), .in3(greater_than_q), .in4(Equal_to_q), .in5(Lesser_than_q),
    .in6(demultiplexer_1_out6), .out(Q), .sel(OP_Code));  // open: in0, in7
endmodule

module Final_Circuit (
  input  in_1,
  input  in_2,
  input  WE,
  input  OE,
  input  [10:0] Instruction_bits,
  input  EN,
  input  ReseT,
  output [3:0] memory_address_A,
  output [3:0] memory_address_B,
  output [2:0] OP_Code,
  output [3:0] out_11
);

  wire a_counter_1_out_put, alu_1_subtractor_bit, and_1_out, binary_to_bcd_converter_1_p2,
       binary_to_bcd_converter_1_p4, binary_to_bcd_converter_2_p2, binary_to_bcd_converter_2_p4,
       binary_to_bcd_converter_3_p2, binary_to_bcd_converter_3_p4, binary_to_bcd_converter_3_p5, CLK_out,
       fsm2_1_dmread, fsm2_1_dmwrite, fsm2_1_enabler_re, fsm2_1_readselect, fsm2_1_reg1we, fsm2_1_reg2we,
       fsm2_1_reg3we, fsm2_1_reset1, fsm2_1_resilt_1_2, fsm2_1_writeselect;
  wire [2:0] forcounter_1_y;
  wire [3:0] alu_1_c_out_multiply, alu_1_result, C_OUT_q, multiplexer_1_out, multiplexer_2_out,
       multiplexer_3_out, ram_2_dout, Register2_q, Register_1_q, test_counter_1_out_4;
  wire [7:0] binary_to_bcd_converter_3_p1;

  Clock CLK (.out(CLK_out));
  RAM #(.addrWidth(3), .dataWidth(11)) ram_1 (
    .addr(forcounter_1_y), .we(WE), .oe(OE), .clk(CLK_out), .din(Instruction_bits),
    .dout({memory_address_A, memory_address_B, OP_Code}));
  a_counter a_counter_1 (.Reset(in_1), .Enabler(EN), .clk(CLK_out), .out_put(a_counter_1_out_put));
  forcounter forcounter_1 (.Reset(in_1), .cntrEnable(in_2), .CLK(CLK_out), .Y(forcounter_1_y));
  FSM2 fsm2_1 (
    .Reset(ReseT), .enabler(EN), .CLK(CLK_out), .readSelect(fsm2_1_readselect),
    .writeSelect(fsm2_1_writeselect), .Reg1WE(fsm2_1_reg1we), .Reg2WE(fsm2_1_reg2we), .Reg3WE(fsm2_1_reg3we),
    .DMread(fsm2_1_dmread), .DMwrite(fsm2_1_dmwrite), .Resilt_1_2(fsm2_1_resilt_1_2), .reset1(fsm2_1_reset1),
    .ENabler_re(fsm2_1_enabler_re));
  test_counter test_counter_1 (
    .Reset(in_1), .clk(a_counter_1_out_put), .en(fsm2_1_enabler_re), .out_4(test_counter_1_out_4));
  Multiplexer #(.width(4)) multiplexer_1 (
    .in0(memory_address_A), .in1(memory_address_B), .out(multiplexer_1_out), .sel(fsm2_1_readselect));
  Multiplexer #(.width(4)) multiplexer_2 (
    .in0(multiplexer_1_out), .in1(test_counter_1_out_4), .out(multiplexer_2_out), .sel(fsm2_1_writeselect));
  Multiplexer #(.width(4)) multiplexer_3 (
    .in0(C_OUT_q), .in1(out_11), .out(multiplexer_3_out), .sel(fsm2_1_resilt_1_2));
  RAM #(.addrWidth(4), .dataWidth(4)) ram_2 (
    .addr(multiplexer_2_out), .we(fsm2_1_dmwrite), .oe(fsm2_1_dmread), .clk(CLK_out),
    .din(multiplexer_3_out), .dout(ram_2_dout));
  Register #(.width(4)) Register_1 (
    .D(ram_2_dout), .en(fsm2_1_reg1we), .clk(CLK_out), .Q(Register_1_q), .clr(fsm2_1_reset1));
  Register #(.width(4)) Register2 (
    .D(ram_2_dout), .en(fsm2_1_reg2we), .clk(CLK_out), .Q(Register2_q), .clr(fsm2_1_reset1));
  ALU alu_1 (
    .A(Register_1_q), .B(Register2_q), .OP(OP_Code), .Result(alu_1_result),
    .c_out_multiply(alu_1_c_out_multiply), .subtractor_bit(alu_1_subtractor_bit));  // open: in_1, c_in_multiplyer, in_6, C_OUT_SUM
  Register_File register_file_1 (
    .WE(fsm2_1_reg3we), .Reset(fsm2_1_reset1), .CLK(CLK_out), .Y(alu_1_result), .OP_Code(OP_Code), .Q(out_11));
  Register #(.width(4)) C_OUT (
    .D(alu_1_c_out_multiply), .en(and_1_out), .clk(CLK_out), .Q(C_OUT_q), .clr(fsm2_1_reset1));
  and and_1 (and_1_out, ~OP_Code[0], OP_Code[1], OP_Code[2]);  // AND_Gate
  _7_Segment_Display u_7_segment_display_1 ();  // open: g, f, a, b, e, d, c, dp
  // BCD_to_7_Segment_decoder bcd_to_7_segment_decoder_1: pin names not known
  // Binary_to_BCD_converter #(.binvalue(4)) binary_to_bcd_converter_1: pin names not known; wires that end beside it: Register_1_q, binary_to_bcd_converter_1_p2, binary_to_bcd_converter_1_p2, binary_to_bcd_converter_1_p4
  _7_Segment_Display u_7_segment_display_2 ();  // open: g, f, a, b, e, d, c, dp
  // BCD_to_7_Segment_decoder bcd_to_7_segment_decoder_2: pin names not known
  // Binary_to_BCD_converter #(.binvalue(4)) binary_to_bcd_converter_2: pin names not known; wires that end beside it: Register2_q, binary_to_bcd_converter_2_p2, binary_to_bcd_converter_2_p2, binary_to_bcd_converter_2_p4
  _7_Segment_Display u_7_segment_display_3 ();  // open: g, f, a, b, e, d, c, dp
  // BCD_to_7_Segment_decoder bcd_to_7_segment_decoder_3: pin names not known; wires that end beside it: binary_to_bcd_converter_1_p4
  _7_Segment_Display u_7_segment_display_4 ();  // open: g, f, a, b, e, d, c, dp
  // BCD_to_7_Segment_decoder bcd_to_7_segment_decoder_4: pin names not known; wires that end beside it: binary_to_bcd_converter_2_p4
  _7_Segment_Display u_7_segment_display_5 ();  // open: g, f, a, b, e, d, c, dp
  // BCD_to_7_Segment_decoder bcd_to_7_segment_decoder_5: pin names not known
  // Binary_to_BCD_converter #(.binvalue(8)) binary_to_bcd_converter_3: pin names not known; wires that end beside it: binary_to_bcd_converter_3_p1, binary_to_bcd_converter_3_p2, binary_to_bcd_converter_3_p2, binary_to_bcd_converter_3_p4, binary_to_bcd_converter_3_p5
  _7_Segment_Display u_7_segment_display_6 ();  // open: g, f, a, b, e, d, c, dp
  // BCD_to_7_Segment_decoder bcd_to_7_segment_decoder_6: pin names not known; wires that end beside it: binary_to_bcd_converter_3_p4
  Splitters splitters_1 (.in_1(out_11), .in_2(C_OUT_q), .out_3(binary_to_bcd_converter_3_p1));
  _7_Segment_Display u_7_segment_display_7 ();  // open: g, f, a, b, e, d, c, dp
  // BCD_to_7_Segment_decoder bcd_to_7_segment_decoder_7: pin names not known; wires that end beside it: binary_to_bcd_converter_3_p5

  // Notes on the sheet:
  //   CLK
  //   Reset
  //   Y
  //   Q
  //   B
  //   A
endmodule
